# Fritzing sketch Nucleo_DCO_Output_VCVS_6th_Bessel _VGND+DCO (saved by Fritzing 0.9.3b)
breadboards: 1
perfboards: 1

parts:
  C1 = Film/Foil Capacitor [capacitance=100nF voltage=35V package="5mm [THT, pp]"]
  R1 = Resistor [tolerance=±5% resistance=100k package=THT]
  R2 = Rotary Potentiometer (Small) [maximum_resistance=100kΩ package=THT]
  IC1 = Dual Op-Amp [package=dip08]
  R3 = Resistor [tolerance=±5% resistance=3.3k package=THT]
  R4 = Resistor [tolerance=±5% resistance=12k package=THT]
  C2 = Film/Foil Capacitor [capacitance=100nF voltage=35V package="5mm [THT, pp]"]
  C3 = Film/Foil Capacitor [capacitance=100nF voltage=35V package="5mm [THT, pp]"]
  R5 = Resistor [tolerance=±5% resistance=20k package=THT]
  R6 = Resistor [tolerance=±5% resistance=10k package=THT]
  IC2 = Dual Op-Amp [package=dip08]
  R7 = Resistor [tolerance=±5% resistance=6.8k package=THT]
  R8 = Resistor [tolerance=±5% resistance=12k package=THT]
  R9 = Resistor [tolerance=±5% resistance=3.9k package=THT]
  R10 = Resistor [tolerance=±5% resistance=12k package=THT]
  C4 = Film/Foil Capacitor [capacitance=100nF voltage=35V package="5mm [THT, pp]"]
  C5 = Film/Foil Capacitor [capacitance=100nF voltage=35V package="5mm [THT, pp]"]
  C6 = Film/Foil Capacitor [capacitance=100nF voltage=35V package="5mm [THT, pp]"]
  C7 = Film/Foil Capacitor [capacitance=100nF voltage=35V package="5mm [THT, pp]"]
  C8 = Electrolytic Capacitor [capacitance=1µF package="100 mil [THT, electrolytic]"]
  R11 = Resistor [tolerance=±5% resistance=10k package=THT]
  C9 = Electrolytic Capacitor [capacitance=1µF package="100 mil [THT, electrolytic]"]
  R12 = Resistor [tolerance=±5% resistance=10k package=THT]
  C10 = Ceramic Capacitor [capacitance=100nF package="100 mil [THT, multilayer]"]
  C11 = Ceramic Capacitor [capacitance=100nF package="100 mil [THT, multilayer]"]
  C12 = Ceramic Capacitor [capacitance=100nF package="100 mil [THT, multilayer]"]
  C13 = Ceramic Capacitor [capacitance=100nF package="100 mil [THT, multilayer]"]
  C14 = Electrolytic Capacitor [capacitance=1µF package="100 mil [THT, electrolytic]"]
  C15 = Electrolytic Capacitor [capacitance=1µF package="100 mil [THT, electrolytic]"]
  U1 = mystery part, 3 pins [chip_label=TLE2426]
  R13 = Resistor [tolerance=±5% resistance=100 package=THT]
  R14 = Resistor [tolerance=±5% resistance=100 package=THT]
  C16 = Electrolytic Capacitor [capacitance=1µF package="100 mil [THT, electrolytic]"]
  VCC1 = Battery block 9V

nets:
  N1: C1.-, R2.wiper
  N2: C1.+, R1.Pin_0, IC1.A_+IN
  N3: R1.Pin_1, C3.-, R6.Pin_1, C5.+, C6.-, C10.0, C11.0, C12.1, C13.1, C14.-, C15.+, U1.pin1
  N4: R2.leg2, IC1.A_V-, IC2.A_V-, R11.Pin_1, R12.Pin_1, C12.0, C13.0, C15.-, U1.pin2, C16.-, VCC1.-
  N5: IC1.A_OUT, R4.Pin_1, R5.Pin_0, R14.Pin_0
  N6: IC1.A_-IN, R5.Pin_1, R6.Pin_0
  N7: IC1.B_+IN, R3.Pin_0, C3.+
  N8: IC1.B_-IN, IC1.B_OUT, C2.+, R10.Pin_1
  N9: IC1.A_V+, IC2.A_V+, C10.1, C11.1, C14.+, U1.pin3, C16.+, VCC1.+
  N10: R3.Pin_1, R4.Pin_0, C2.-
  N11: IC2.A_OUT, IC2.A_-IN, R8.Pin_1, C4.-
  N12: IC2.A_+IN, R9.Pin_0, C5.-
  N13: IC2.B_+IN, R7.Pin_0, C6.+
  N14: IC2.B_-IN, IC2.B_OUT, C7.+, R13.Pin_0
  N15: R7.Pin_1, R8.Pin_0, C7.-
  N16: R9.Pin_1, R10.Pin_0, C4.+
  N17: C8.-, R11.Pin_0
  N18: C8.+, R13.Pin_1
  N19: C9.-, R12.Pin_0
  N20: C9.+, R14.Pin_1

notes:
  IN
  VEE
  VGND
  VGND
  VCC
  OUT
  BYPASS
  Nucleo DCO
  Out
  VIN
  +9V
