# Fritzing sketch ADC_VREF_Test01 (saved by Fritzing 0.9.3b)
breadboards: 1

parts:
  J1 = STM32 Nucleo boards
  R2 = Resistor [tolerance=±5% resistance=33k package=THT]
  R3 = Resistor [tolerance=±5% resistance=68k package=THT]

nets:
  N1: J1.A0, R2.Pin_0, R3.Pin_0
  N2: J1.GND, R2.Pin_1

notes:
  1.25V ~ 12V
  Variable PSU
