# Fritzing sketch GateGen01 (saved by Fritzing 0.9.3b)
breadboards: 1

parts:
  パーツ1 = Arduino Nano (Rev3.0) (ICSP)
  R1 = Rotary Potentiometer (Small) [maximum_resistance=100kΩ package=THT]
  R2 = Rotary Potentiometer (Small) [maximum_resistance=100kΩ package=THT]
  C1 = Electrolytic Capacitor [capacitance=1µF package="100 mil [THT, electrolytic]"]
  R3 = Rotary Potentiometer (Small) [maximum_resistance=100kΩ package=THT]
  TRS1 = Audio Jack (TRS) 3.5mm [package="4Ucon 08780 [THT]"]
  TRS2 = Audio Jack (TRS) 3.5mm [package="PG203J [THT]"]

nets:
  N1: パーツ1.GND, R1.leg1, R2.leg1, C1.-, R3.leg1, TRS1.Sleeve, TRS2.Sleeve
  N2: パーツ1.D3, TRS2.Tip
  N3: パーツ1.D5, TRS1.Tip
  N4: パーツ1.5V, R1.leg2, R2.leg2, C1.+, R3.leg2
  N5: パーツ1.A2, R3.wiper
  N6: パーツ1.A1, R1.wiper
  N7: パーツ1.A0, R2.wiper

notes:
  Freq
  PW
  GND
  +5V
  KIK01 Sync
  SYS-DAS01
  Gate
