# Fritzing sketch Nucleo_DCO_PSU (saved by Fritzing 0.9.3b)
breadboards: 1

parts:
  C1 = Electrolytic Capacitor [capacitance=1µF package="100 mil [THT, electrolytic]"]
  U1 = Voltage Regulator - 5V [package="TO220 [THT]"]
  C2 = Ceramic Capacitor [capacitance=100nF package="100 mil [THT, multilayer]"]
  C3 = Ceramic Capacitor [capacitance=100nF package="100 mil [THT, multilayer]"]
  D1 = Schottky Diode [part_number=1N5817 package="300 mil [THT]"]
  C4 = Electrolytic Capacitor [capacitance=1µF package="100 mil [THT, electrolytic]"]
  R1 = Resistor [tolerance=±5% resistance=1k package=THT]
  LED1 = LED - 3mm [color="Green (570nm)" package="3 mm [THT]"]

nets:
  N1: C1.-, U1.GND, C2.0, C3.1, C4.-, LED1.cathode
  N2: C1.+, U1.input_voltage, C2.1, D1.cathode, R1.Pin_0
  N3: U1.output_voltage, C3.0, D1.anode, C4.+
  N4: R1.Pin_1, LED1.anode

notes:
  GND
  IN
  GND
  OUT
