# Fritzing sketch Nucleo_DCO_Test20_Single_Supply_OutputBoard (saved by Fritzing 0.9.3b)
breadboards: 1

parts:
  Power_plug1 = Power plug
  TRS1 = Audio Jack (TRS) 3.5mm [package="4Ucon 08780 [THT]"]
  IC1 = Dual Op-Amp [package=dip08]
  R1 = Rotary Potentiometer (Small) [maximum_resistance=100kΩ package=THT]
  C1 = Ceramic Capacitor [capacitance=100nF package="100 mil [THT, multilayer]"]
  C2 = Electrolytic Capacitor [capacitance=1µF package="100 mil [THT, electrolytic]"]
  R2 = Resistor [tolerance=±5% resistance=12k package=THT]
  R3 = Resistor [tolerance=±5% resistance=3.3k package=THT]
  C3 = Electrolytic Capacitor [capacitance=1µF package="100 mil [THT, electrolytic]"]
  R4 = Resistor [tolerance=±5% resistance=100k package=THT]

nets:
  N1: Power_plug1.GND, TRS1.Sleeve, IC1.A_+IN, IC1.A_V-, R1.leg2, C1.0, C2.-, R3.Pin_0, R4.Pin_0
  N2: Power_plug1.VCC, IC1.A_V+, C1.1, C2.+, R2.Pin_0
  N3: TRS1.Tip, C3.-, R4.Pin_1
  N4: IC1.A_OUT, IC1.A_-IN
  N5: IC1.B_+IN, R1.wiper
  N6: IC1.B_-IN, IC1.B_OUT, C3.+
  N7: R2.Pin_1, R3.Pin_1

notes:
  GND
  +12V
  DC+12V IN
  Nucleo
  A2
  OUT
  Nucleo
  VIN / GND
  Nucleo
  PB1
  GND
  NC
